# Fritzing sketch blockblast (saved by Fritzing 0.9.4b)
breadboards: 1

parts:
  TTGO_T-Display = ESP32-TTGO-T-DISPLAY
  Joystick_KY-023 = Black Joystick KY-023
  Trimmer_Pot = TRIMPOT [package=3386u]
  Pushbutton = Pushbutton [package="[THT]"]

nets:
  N1: TTGO_T-Display.G-1, TTGO_T-Display.G-2, TTGO_T-Display.G-10, TTGO_T-Display.G-11, TTGO_T-Display.G-14, Joystick_KY-023.GND, Trimmer_Pot.CW, Pushbutton.Pin_3, Pushbutton.Pin_4
  N2: TTGO_T-Display.2, Pushbutton.Pin_1, Pushbutton.Pin_2
  N3: TTGO_T-Display.15, Trimmer_Pot.WIPER
  N4: TTGO_T-Display.3V, Joystick_KY-023.+5V, Trimmer_Pot.CCW
  N5: TTGO_T-Display.33, Joystick_KY-023.SW
  N6: TTGO_T-Display.32, Joystick_KY-023.VRy
  N7: TTGO_T-Display.39, Joystick_KY-023.VRx

custom parts:
  ESP32-TTGO-T-DISPLAY: LILYGO TTGO T-Display GD32VF103CBT6 Main Chip ST7789 1.14 Inch IPS 240x135 Resolution Minimalist Development Board.
  Black Joystick KY-023: Description: The joystick is a combination of 2 analoog potentiometer and a digital switch. Arduino GND --> Module pin - Arduino +5V --> Module pin +5V Arduino Analoog 0 --> Module VRx Arduino Analoog 1 --> Module VRy Arduino Digital --> Module SW Dimensions: 1" x 1.25"
